// Logisim project CS115B.circ as structural Verilog: 4 circuits, main circuit xor
module \xor  (
  input  x,
  input  y,
  output \output 
);

  wire and_1_out, and_2_out, not_1_out, not_2_out;

  not not_1 (not_1_out, x);
  not not_2 (not_2_out, y);
  and and_1 (and_1_out, not_1_out, y);
  and and_2 (and_2_out, x, not_2_out, not_2_out);
  or or_1 (\output , and_1_out, and_2_out);
endmodule

module full_adder (
  input  A,
  input  B,
  input  Ci,
  output S,
  output Co
);

  wire and_1_out, and_2_out, xor_1_out;

  xor xor_1 (xor_1_out, A, B);
  and and_1 (and_1_out, A, B);
  xor xor_2 (S, xor_1_out, Ci);
  and and_2 (and_2_out, xor_1_out, Ci);
  xor xor_3 (Co, and_2_out, and_1_out);
endmodule

module S_R_Latch (
  input  S,
  input  R,
  output not_Q,
  output Q
);

  nor nor_1 (not_Q, S, Q);
  nor nor_2 (Q, not_Q, R);
endmodule

module D_Latch (
  input  D,
  input  Strobe,
  output not_Q,
  output Q
);

  wire and_1_out, and_2_out, not_1_out;

  not not_1 (not_1_out, D);
  and and_1 (and_1_out, D, Strobe);
  and and_2 (and_2_out, not_1_out, Strobe, Strobe);
  S_R_Latch s_r_latch_1 (.S(and_1_out), .R(and_2_out), .not_Q(not_Q), .Q(Q));
endmodule
