// Logisim project lab7.circ as structural Verilog: 3 circuits, main circuit MyXOR
module MyXOR (
  input  x,
  input  y,
  output x_XOR_y
);

  wire and_1_out, and_2_out, not_1_out, not_2_out;

  not not_1 (not_1_out, x);
  not not_2 (not_2_out, y);
  and and_1 (and_1_out, not_1_out, y);
  and and_2 (and_2_out, x, not_2_out);
  or or_1 (x_XOR_y, and_1_out, and_2_out);

  // Notes on the sheet:
  //   Here is a location to build an XOR circuit
  //   We already implemented this circuit in class.  Copy it here.
endmodule

module FullAdder (
  input  X,
  input  Y,
  input  CarryIn,
  output sum,
  output CarryOut
);

  wire and_1_out, and_2_out, myxor_1_x_xor_y;

  and and_1 (and_1_out, X, Y);
  MyXOR myxor_1 (.x(Y), .y(X), .x_XOR_y(myxor_1_x_xor_y));
  MyXOR myxor_2 (.x(CarryIn), .y(myxor_1_x_xor_y), .x_XOR_y(sum));
  and and_2 (and_2_out, myxor_1_x_xor_y, CarryIn);
  MyXOR myxor_3 (.x(and_2_out), .y(and_1_out), .x_XOR_y(CarryOut));
endmodule

module _4_bit_Ripple_Carry_Adder (
  input  Y3,
  input  Y2,
  input  Y1,
  input  Y0,
  input  X3,
  input  X2,
  input  X1,
  input  X0,
  output Sum4,
  output Sum3,
  output Sum2,
  output Sum1,
  output Sum0
);

  wire fulladder_2_carryout, fulladder_3_carryout, fulladder_4_carryout;

  FullAdder fulladder_1 (.X(Y3), .Y(X3), .CarryIn(fulladder_2_carryout), .sum(Sum3), .CarryOut(Sum4));
  FullAdder fulladder_2 (.X(X2), .Y(Y2), .CarryIn(fulladder_3_carryout), .sum(Sum2), .CarryOut(fulladder_2_carryout));
  FullAdder fulladder_3 (.X(X1), .Y(Y1), .CarryIn(fulladder_4_carryout), .sum(Sum1), .CarryOut(fulladder_3_carryout));
  FullAdder fulladder_4 (.X(Y0), .Y(X0), .CarryIn(1'b0), .sum(Sum0), .CarryOut(fulladder_4_carryout));
endmodule
